# Fritzing sketch demo2 (saved by Fritzing 0.9.3b)
breadboards: 1

parts:
  Part1 = Adafruit T-Cobbler Plus [part_number="Adafruit #1989 and #2028"]
  LED3 = smd LED [color="Yellow (585nm)" package="0805 [SMD]"]
  LED4 = smd LED [color="Red (633nm)" package="1206 [SMD]"]
  LED5 = smd LED [color="Green (570nm)" package="1206 [SMD]"]
  LED6 = smd LED [color="Green (570nm)" package="1206 [SMD]"]
  LED7 = smd LED [color="Yellow (585nm)" package="1206 [SMD]"]
  LED8 = smd LED [color="Red (633nm)" package="1206 [SMD]"]
  S1 = Momentary Switch [package=ksa_sealed_tac_switch]
  R1 = Resistor [tolerance=±5% resistance=220 package=THT]
  R2 = Resistor [tolerance=±5% resistance=220 package=THT]
  R3 = Resistor [tolerance=±5% resistance=220 package=THT]
  R4 = Resistor [tolerance=±5% resistance=220 package="0402 [SMD]"]
  R5 = Resistor [tolerance=±5% resistance=220 package=THT]
  R6 = Resistor [tolerance=±5% resistance=220 package=THT]
  R7 = Resistor [tolerance=±5% resistance=220 package=THT]
  PIR1 = PIR sensor

nets:
  GND: Part1.GND, R1.Pin_0, R2.Pin_1, R3.Pin_0, R4.Pin_0, R5.Pin_1, R6.Pin_1, R7.Pin_1, PIR1.GND
  N1: Part1.+3.3V_2, S1.2
  N2: Part1.GPIO6, LED6.anode
  N3: Part1.GPIO13, LED7.anode
  N4: Part1.GPIO19, S1.3, R4.Pin_1
  N5: Part1.GPIO26, LED8.anode
  +5V: Part1.+5V, PIR1.VDD
  N6: Part1.GPIO23, PIR1.SIG
  N7: Part1.GPIO16, LED4.anode
  N8: Part1.GPIO20, LED3.anode
  N9: Part1.GPIO21, LED5.anode
  N10: LED3.cathode, R5.Pin_0
  N11: LED4.cathode, R7.Pin_0
  N12: LED5.cathode, R6.Pin_0
  N13: LED6.cathode, R1.Pin_1
  N14: LED7.cathode, R2.Pin_0
  N15: LED8.cathode, R3.Pin_1

custom parts:
  Adafruit T-Cobbler Plus: The Raspberry Pi has landed on the Maker World like a 40-GPIO pinned, quad-USB ported, credit card sized bomb of DIY joy. And while you can use most of our great Model B accessories by hooking up our downgrade cable, its probably a good time to upgrade your set up and accessorize using all of the 40 pins. That's why we now carry the Assembled Adafruit Pi T-Cobbler Plus - Breakout + Cable for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
